// Logisim project PROJ.circ as structural Verilog: 8 circuits, main circuit main
module main (
);

  wire alu_1_flag_0;
  wire [7:0] registers_1_bus_out, undriven;

  CONTROL_LOGIC control_logic_1 ();  // open: INSTRUCTION, REGISTERS_WR, REGISTERS_OE, ALU_OE, ALU1_WR, ALU2_WR, ROM_OE, RAM_STORE, RAM_LOAD
  REGISTERS registers_1 (
    .BUS_IN(registers_1_bus_out), .BUS_OUT(registers_1_bus_out));  // open: RESET, REGISTERS_WR, REGISTERS_OE
  ALU alu_1 (
    .in_1(registers_1_bus_out), .ALU_DATA(registers_1_bus_out), .FLAG_0(alu_1_flag_0));  // open: ALU1_WR, ALU2_WR, ALU_OE
  ROM_1 rom_1_1 (.ROM_BE(undriven), .ROM_BD(registers_1_bus_out));  // open: ROM_OE
  RAM_1 ram_1_1 (.BD_IN(registers_1_bus_out), .BE(undriven), .BD_OUT(registers_1_bus_out));  // open: OE, WR
  DotMatrix #(.inputtype("row"), .matrixcols(8), .matrixrows(1)) dotmatrix_1 (.row0(registers_1_bus_out));
  LED led_1 (.in(alu_1_flag_0));
endmodule

module ALU (
  input  [7:0] in_1,
  input  ALU1_WR,
  input  ALU2_WR,
  input  ALU_OE,
  output [7:0] ALU_DATA,
  output FLAG_0
);

  wire or_1_out;
  wire [7:0] adder_1_out, ALU1_q, ALU2_q, controlled_buffer_1_out;

  or or_1 (or_1_out, ALU2_WR, ALU1_WR);
  Register #(.trigger("falling")) ALU1 (
    .D(controlled_buffer_1_out), .en(1'b1), .clk(ALU1_WR), .Q(ALU1_q));  // open: clr
  Register #(.trigger("falling")) ALU2 (
    .D(controlled_buffer_1_out), .en(1'b1), .clk(ALU2_WR), .Q(ALU2_q));  // open: clr
  Adder adder_1 (.a(ALU1_q), .b(ALU2_q), .out(adder_1_out));  // open: cin, cout
  assign controlled_buffer_1_out = ALU_OE ? adder_1_out : 8'bz;  // Controlled_Buffer controlled_buffer_1
  assign controlled_buffer_1_out = or_1_out ? in_1 : 8'bz;  // Controlled_Buffer controlled_buffer_2
  Comparator comparator_1 (.a(adder_1_out), .b({8{1'b0}}), .eq(FLAG_0));  // open: gt, lt
  assign ALU_DATA = ALU_OE ? controlled_buffer_1_out : 8'bz;  // Controlled_Buffer controlled_buffer_3
endmodule

module REGISTERS (
  input  [7:0] REGISTERS_WR,
  input  [7:0] BUS_IN,
  input  [7:0] REGISTERS_OE,
  input  RESET,
  output [7:0] BUS_OUT
);

  wire or_1_out, or_2_out;
  wire [7:0] controlled_buffer_1_out, register_1_q, register_2_q, register_3_q, register_4_q, register_5_q,
       register_6_q, register_7_q, register_8_q;

  Register #(.trigger("falling")) register_1 (
    .D(controlled_buffer_1_out), .en(1'b1), .clk(REGISTERS_WR[0]), .Q(register_1_q), .clr(RESET));
  Register #(.trigger("falling")) register_2 (
    .D(controlled_buffer_1_out), .en(1'b1), .clk(REGISTERS_WR[1]), .Q(register_2_q), .clr(RESET));
  Register #(.trigger("falling")) register_3 (
    .D(controlled_buffer_1_out), .en(1'b1), .clk(REGISTERS_WR[2]), .Q(register_3_q), .clr(RESET));
  Register #(.trigger("falling")) register_4 (
    .D(controlled_buffer_1_out), .en(1'b1), .clk(REGISTERS_WR[3]), .Q(register_4_q), .clr(RESET));
  Register #(.trigger("falling")) register_5 (
    .D(controlled_buffer_1_out), .en(1'b1), .clk(REGISTERS_WR[4]), .Q(register_5_q), .clr(RESET));
  Register #(.trigger("falling")) register_6 (
    .D(controlled_buffer_1_out), .en(1'b1), .clk(REGISTERS_WR[5]), .Q(register_6_q), .clr(RESET));
  Register #(.trigger("falling")) register_7 (
    .D(controlled_buffer_1_out), .en(1'b1), .clk(REGISTERS_WR[6]), .Q(register_7_q), .clr(RESET));
  Register #(.trigger("falling")) register_8 (
    .D(controlled_buffer_1_out), .en(1'b1), .clk(REGISTERS_WR[7]), .Q(register_8_q), .clr(RESET));
  or or_1 (or_1_out, REGISTERS_WR[0], REGISTERS_WR[1], REGISTERS_WR[2], REGISTERS_WR[3], REGISTERS_WR[4], REGISTERS_WR[5], REGISTERS_WR[6], REGISTERS_WR[7]);
  assign controlled_buffer_1_out = REGISTERS_OE[0] ? register_1_q : 8'bz;  // Controlled_Buffer controlled_buffer_1
  assign controlled_buffer_1_out = REGISTERS_OE[1] ? register_2_q : 8'bz;  // Controlled_Buffer controlled_buffer_2
  assign controlled_buffer_1_out = REGISTERS_OE[2] ? register_3_q : 8'bz;  // Controlled_Buffer controlled_buffer_3
  assign controlled_buffer_1_out = REGISTERS_OE[3] ? register_4_q : 8'bz;  // Controlled_Buffer controlled_buffer_4
  assign controlled_buffer_1_out = REGISTERS_OE[4] ? register_5_q : 8'bz;  // Controlled_Buffer controlled_buffer_5
  assign controlled_buffer_1_out = REGISTERS_OE[5] ? register_6_q : 8'bz;  // Controlled_Buffer controlled_buffer_6
  assign controlled_buffer_1_out = REGISTERS_OE[6] ? register_7_q : 8'bz;  // Controlled_Buffer controlled_buffer_7
  assign controlled_buffer_1_out = REGISTERS_OE[7] ? register_8_q : 8'bz;  // Controlled_Buffer controlled_buffer_8
  assign controlled_buffer_1_out = or_1_out ? BUS_IN : 8'bz;  // Controlled_Buffer controlled_buffer_9
  assign BUS_OUT = or_2_out ? controlled_buffer_1_out : 8'bz;  // Controlled_Buffer controlled_buffer_10
  or or_2 (or_2_out, REGISTERS_OE[7], REGISTERS_OE[6], REGISTERS_OE[5], REGISTERS_OE[4], REGISTERS_OE[3], REGISTERS_OE[2], REGISTERS_OE[1], REGISTERS_OE[0]);
endmodule

module ROM_1 (
  input  [7:0] ROM_BE,
  input  ROM_OE,
  output [7:0] ROM_BD
);

  wire [7:0] rom_1_data;

  ROM rom_1 (.addr(ROM_BE), .data(rom_1_data));
  assign ROM_BD = ROM_OE ? rom_1_data : 8'bz;  // Controlled_Buffer controlled_buffer_1

  // Notes on the sheet:
  //   contents of rom_1 (hex, n*v repeats v):
  //   2 a1 1e 12 91 55 dd ff
endmodule

module INSTRUCTION_REGISTER (
  input  [7:0] in_1
);

  Register #(.width(16)) register_1 ();  // open: D, en, clk, Q, clr
endmodule

module PROGRAM_COUNTER (
  input  RESET,
  input  LOAD_NOTCOUNT,
  input  LOAD_INC,
  input  [7:0] BD,
  input  OE,
  output [7:0] BE
);

  wire [7:0] counter_1_q;

  Counter counter_1 (
    .clr(RESET), .load(LOAD_NOTCOUNT), .up(1'b1), .count(1'b1), .clk(LOAD_INC), .D(BD), .Q(counter_1_q));  // open: carry
  assign BE = OE ? counter_1_q : 8'bz;  // Controlled_Buffer controlled_buffer_1
endmodule

module CONTROL_LOGIC (
  input  [15:0] INSTRUCTION,
  output [1:0] REGISTERS_WR,
  output [1:0] REGISTERS_OE,
  output ALU_OE,
  output ALU1_WR,
  output ALU2_WR,
  output ROM_OE,
  output RAM_STORE,
  output RAM_LOAD
);
endmodule

module RAM_1 (
  input  [7:0] BE,
  input  OE,
  input  [7:0] BD_IN,
  input  WR,
  output [7:0] BD_OUT
);

  wire [7:0] controlled_buffer_2_out;

  assign BD_OUT = OE ? controlled_buffer_2_out : 8'bz;  // Controlled_Buffer controlled_buffer_1
  assign controlled_buffer_2_out = WR ? BD_IN : 8'bz;  // Controlled_Buffer controlled_buffer_2
  RAM #(.trigger("falling")) ram_1 (
    .addr(BE), .we(WR), .oe(OE), .din(controlled_buffer_2_out), .dout(controlled_buffer_2_out));  // open: clk
endmodule
